# Fritzing sketch FlashRide_Transmitter_PCB (saved by Fritzing 0.9.2b)
circuit board: 3.04561cm x 7.17129cm
breadboards: 1

parts:
  S1 = SWITCH-MOMENTARY-2 [package=tactile-pth-12mm]
  S4 = SWITCH-MOMENTARY-2 [package=tactile-pth-12mm]
  S5 = SWITCH-MOMENTARY-2 [package=tactile-pth-12mm]
  R1 = Resistor [tolerance=±5% resistance=220 package=THT]
  R2 = Resistor [tolerance=±5% resistance=220 package=THT]
  R3 = Resistor [tolerance=±5% resistance=220 package=THT]
  BAT1 = Battery Holders [package=battcon_12mm]
  U1 = XBEE-1 [package=xbee-silk]

nets:
  N1: S1.1, R1.Pin_1, U1.DIO1
  N2: S1.2, S4.2, S5.2, BAT1.-, U1.VDD
  N3: S4.1, R2.Pin_1, U1.DIO0
  N4: S5.1, R3.Pin_1, U1.DIO2
  N5: R1.Pin_0, R2.Pin_0, R3.Pin_0, BAT1.+, U1.GND
