# Fritzing sketch receiver pcb (saved by Fritzing 0.7.5b)

parts:
  XBEE = XBee
  R1 = Resistor [tolerance=±5% resistance=51k package=THT]
  R2 = Resistor [tolerance=±5% resistance=51k package=THT]
  R3 = Resistor [tolerance=±5% resistance=51k package=THT]
  C1 = Electrolytic Capacitor [capacitance=1µF package="100 mil [THT, electrolytic]"]
  C2 = Electrolytic Capacitor [capacitance=1µF package="100 mil [THT, electrolytic]"]
  C3 = Electrolytic Capacitor [capacitance=1µF package="100 mil [THT, electrolytic]"]
  ATTINY84 = IC, DIP package, 14 pins [chip_label=ATTINY84 spacing=300mil]
  VCC = Battery
  R4 = Resistor [tolerance=±5% resistance=120 package=THT]
  to_LEDs = male pin header, 4 pins [form="♂ (male)"]
  R5 = Resistor [tolerance=±5% resistance=120 package=THT]
  R6 = Resistor [tolerance=±5% resistance=120 package=THT]

nets:
  N1: XBEE.VCC, ATTINY84.pin1, VCC.+
  N2: XBEE.GND, C1.-, C2.-, C3.-, ATTINY84.pin14, VCC.-, to_LEDs.pin1
  N3: XBEE.pin18, R3.Pin_0
  N4: XBEE.pin19, R2.Pin_0
  N5: XBEE.pin20, R1.Pin_0
  N6: R1.Pin_1, C3.+, ATTINY84.pin8
  N7: R2.Pin_1, C2.+, ATTINY84.pin9
  N8: R3.Pin_1, C1.+, ATTINY84.pin10
  N9: ATTINY84.pin11, R6.Pin_0
  N10: ATTINY84.pin12, R5.Pin_0
  N11: ATTINY84.pin13, R4.Pin_0
  N12: R4.Pin_1, to_LEDs.pin4
  N13: to_LEDs.pin2, R6.Pin_1
  N14: to_LEDs.pin3, R5.Pin_1

notes:
  Flash Ride
