# Fritzing sketch receiver soldered_circuit diag (saved by Fritzing 0.7.5b)
perfboards: 1

parts:
  R1 = Resistor [tolerance=±5% resistance=51k package=THT]
  R2 = Resistor [tolerance=±5% resistance=51k package=THT]
  R3 = Resistor [tolerance=±5% resistance=51k package=THT]
  Arduino_pins_D0-D7 = female pin header, 8 pins [form="♀ (female)"]
  Arduino_power_pins = female pin header, 8 pins [form="♀ (female)"]
  U1 = XBee
  Arduino_pins_D8-D13 = female pin header, 10 pins [form="♀ (female)"]
  Arduino_pins_A0-A5 = female pin header, 6 pins [form="♀ (female)"]  # not connected
  C1 = Electrolytic Capacitor [capacitance=1µF package="100 mil [THT, electrolytic]"]
  C2 = Electrolytic Capacitor [capacitance=1µF package="100 mil [THT, electrolytic]"]
  C3 = Electrolytic Capacitor [capacitance=1µF package="100 mil [THT, electrolytic]"]
  R4 = Resistor [tolerance=±5% resistance=120 package=THT]
  R5 = Resistor [tolerance=±5% resistance=120 package=THT]
  R6 = Resistor [tolerance=±5% resistance=120 package=THT]
  To_LEDs = male pin header, 4 pins [form="♂ (male)"]

nets:
  N1: R1.Pin_0, Arduino_pins_D0-D7.pin6, C1.+
  N2: R1.Pin_1, U1.pin18
  N3: R2.Pin_0, Arduino_pins_D0-D7.pin5, C2.+
  N4: R2.Pin_1, U1.pin19
  N5: R3.Pin_0, Arduino_pins_D0-D7.pin4, C3.+
  N6: R3.Pin_1, U1.pin20
  GND: Arduino_power_pins.pin2, U1.GND, Arduino_pins_D8-D13.pin4, C1.-, C2.-, C3.-, To_LEDs.pin1
  N7: Arduino_power_pins.pin5, U1.VCC
  N8: Arduino_pins_D8-D13.pin5, R4.Pin_0
  N9: Arduino_pins_D8-D13.pin6, R5.Pin_0
  N10: Arduino_pins_D8-D13.pin7, R6.Pin_0
  N11: R4.Pin_1, To_LEDs.pin4
  N12: R5.Pin_1, To_LEDs.pin3
  N13: R6.Pin_1, To_LEDs.pin2
